# Fritzing sketch robo rob (saved by Fritzing 0.8.7b)
circuit board: 12cm x 8cm
breadboards: 1

parts:
  ESP_8266 = NodeMCU V1.0
  ATMega328 = Arduino Nano (Rev3.0)
  IN_5V_GND = screw terminal, 2 pins
  A1_A0 = female pin header, 2 pins [form="♀ (female)"]
  M-R = female pin header, 2 pins [form="♀ (female)"]
  M-L = female pin header, 2 pins [form="♀ (female)"]
  J-RX = female pin header, 2 pins [form="♀ (female)"]
  BTN = female pin header, 2 pins [form="♀ (female)"]
  IND = female pin header, 2 pins [form="♀ (female)"]
  11_10_9 = female pin header, 3 pins [form="♀ (female)"]
  13_12 = female pin header, 2 pins [form="♀ (female)"]
  I2C = female pin header, 2 pins [form="♀ (female)"]
  A7_A6_A5_A4 = female pin header, 4 pins [form="♀ (female)"]
  5V = female pin header, 4 pins [form="♀ (female)"]
  GND = female pin header, 4 pins [form="♀ (female)"]
  12V_GND = screw terminal, 2 pins
  12V_GND_2 = screw terminal, 2 pins
  12V_GND_3 = screw terminal, 2 pins
  12V_GND_4 = screw terminal, 2 pins
  IN_12V_GND = screw terminal, 2 pins
  8_7 = female pin header, 2 pins [form="♀ (female)"]
  S-Front = female pin header, 4 pins [form="♀ (female)"]
  S-Back = female pin header, 4 pins [form="♀ (female)"]

nets:
  N1: ESP_8266.D1, ATMega328.A4, I2C.pin2
  N2: ESP_8266.D2, ATMega328.A5, I2C.pin1
  N3: ESP_8266.D3, IND.pin1
  N4: ESP_8266.D4, BTN.pin2
  GND: ESP_8266.GND, ATMega328.GND, IN_5V_GND.pin2, BTN.pin1, IND.pin2, GND.pin1, GND.pin2, GND.pin3, GND.pin4, S-Front.pin1, S-Back.pin1
  N5: ESP_8266.D5, M-R.pin2
  N6: ESP_8266.D6, M-R.pin1
  N7: ESP_8266.D7, M-L.pin2
  N8: ESP_8266.D8, M-L.pin1
  N9: ESP_8266.RX, J-RX.pin1
  VIN: ESP_8266.Vin, ATMega328.VIN, IN_5V_GND.pin1, 5V.pin1, 5V.pin2, 5V.pin3, 5V.pin4, S-Front.pin4, S-Back.pin4
  N10: ATMega328.D2, S-Back.pin2
  N11: ATMega328.D3, S-Back.pin3
  N12: ATMega328.D4, S-Front.pin2
  N13: ATMega328.D5, S-Front.pin3
  N14: ATMega328.D6, J-RX.pin2
  N15: ATMega328.D7, 8_7.pin1
  N16: ATMega328.D8, 8_7.pin2
  N17: ATMega328.D9, 11_10_9.pin1
  N18: ATMega328.D10, 11_10_9.pin2
  N19: ATMega328.D11/MOSI, 11_10_9.pin3
  N20: ATMega328.D12/MISO, 13_12.pin1
  N21: ATMega328.A7, A1_A0.pin1
  N22: ATMega328.A6, A1_A0.pin2
  N23: ATMega328.A3, A7_A6_A5_A4.pin1
  N24: ATMega328.A2, A7_A6_A5_A4.pin2
  N25: ATMega328.A1, A7_A6_A5_A4.pin3
  N26: ATMega328.A0, A7_A6_A5_A4.pin4
  N27: ATMega328.D13/SCK, 13_12.pin2
  N28: 12V_GND.pin1, 12V_GND_2.pin1, 12V_GND_3.pin1, 12V_GND_4.pin1, IN_12V_GND.pin1
  N29: 12V_GND.pin2, 12V_GND_2.pin2, 12V_GND_3.pin2, 12V_GND_4.pin2, IN_12V_GND.pin2

notes:
  Stepper Connection
  Main Motor Driver
  Ultrasonc Front
  Ultrasonc Back
  Limit Switch for Stepper
  5v power supply
  Designed by Supriya Das
  28/07/2020
  Robo Rob
  PWM Pin
  12v Power Array
  5v power array
  smart robot
  Developed by: Supriya and Raj
  Node MCU 12E
  Arduino NANO

custom parts:
  NodeMCU V1.0: ESP8266 based NodeMCU
